# Fritzing sketch LCD (saved by Fritzing 0.9.2b)
breadboards: 1

parts:
  U1 = LCD-16X2 [package=lcd-16x2]
  1K = POT [package=pot_alpha_rv16af-20]
  Parte1 = Arduino Mega ADK (Rev3)

nets:
  VSS: U1.VSS, U1.R_W, U1.K, 1K.A, Parte1.GND
  VDD: U1.VDD, U1.A, 1K.E, Parte1.5V
  N1: U1.VO, 1K.S
  N2: U1.RS, Parte1.D12_PWM
  N3: U1.E, Parte1.D11_PWM
  N4: U1.DB4, Parte1.D10_PWM
  N5: U1.DB5, Parte1.D9_PWM
  N6: U1.DB6, Parte1.D8_PWM
  N7: U1.DB7, Parte1.D7_PWM
